# Fritzing sketch prototype (saved by Fritzing 0.9.3b)
circuit board: 8.46667cm x 5.64444cm
breadboards: 1

parts:
  LED1 = LED - 5mm [color="Red (633nm)" package="5 mm [THT]"]
  LED2 = LED - 5mm [color="Red (633nm)" package="5 mm [THT]"]
  LED3 = LED - 5mm [color="Red (633nm)" package="5 mm [THT]"]
  LED4 = LED - 5mm [color="Red (633nm)" package="5 mm [THT]"]
  LED5 = LED - 5mm [color="Red (633nm)" package="5 mm [THT]"]
  R1 = Resistor [tolerance=±5% resistance=330 package=THT]  # not connected
  R4 = Resistor [tolerance=±5% resistance=330 package=THT]
  R5 = Resistor [tolerance=±5% resistance=330 package=THT]
  R6 = Resistor [tolerance=±5% resistance=330 package=THT]
  R7 = Resistor [tolerance=±5% resistance=330 package=THT]
  S1 = Pushbutton [package="[THT]"]
  S2 = Pushbutton [package="[THT]"]
  R9 = Resistor [tolerance=±5% resistance=220 package=THT]
  VCC1 = 4 x AAA Battery Mount
  LED6 = LED - 5mm [color="Green (555nm)" package="5 mm [THT]"]
  R10 = Resistor [tolerance=±5% resistance=330 package=THT]
  R11 = Resistor [tolerance=±5% resistance=330 package=THT]
  LED7 = LED - 5mm [color="Green (555nm)" package="5 mm [THT]"]
  Composant1 = Arduino Uno (Rev3)
  R8 = Resistor [tolerance=±5% resistance=220 package=THT]

nets (from the pcb view):
  N1: LED1.anode, Composant1.D6_PWM
  N2: LED2.cathode, R7.Pin_1
  N3: LED2.anode, Composant1.D10_PWM/SS
  N4: LED3.cathode, VCC1.-, Composant1.GND
  N5: LED3.anode, Composant1.D9_PWM
  N6: LED4.cathode, R4.Pin_1
  N7: LED4.anode, Composant1.D8
  N8: LED5.cathode, R5.Pin_1
  N9: LED5.anode, Composant1.D7
  N10: R4.Pin_0, R5.Pin_0, R6.Pin_1, R8.Pin_0
  N11: R6.Pin_0, R7.Pin_0, R9.Pin_0
  N12: S1.Pin_1, S1.Pin_2, Composant1.D3_PWM
  N13: S1.Pin_3, S1.Pin_4, S2.Pin_3, S2.Pin_4, R9.Pin_1, Composant1.5V, R8.Pin_1
  N14: S2.Pin_1, S2.Pin_2, Composant1.D2
  N15: VCC1.+, Composant1.VIN
  N16: LED6.cathode, R10.Pin_1
  N17: LED6.anode, Composant1.D5_PWM
  N18: R11.Pin_1, LED7.cathode
  N19: LED7.anode, Composant1.D4
